# Fritzing sketch relayinator (saved by Fritzing 0.9.4)
circuit board: 6.16564cm x 3.07755cm
breadboards: 1

parts:
  J1 = female pin header, 10 pins [form="♀ (female)"]
  J2 = female pin header, 10 pins [form="♀ (female)"]
  IO0_GND_GND_RX_TX_5V = female pin header, 6 pins [form="♀ (female)"]
  J3 = female pin header, 10 pins [form="♀ (female)"]  # not connected
  J4 = female pin header, 10 pins [form="♀ (female)"]  # not connected
  OLED1 = OLED 128x64 I2C Monochrome Display
  GND_CTS_VCC_TX_RX_DTR = female pin header, 6 pins [form="♀ (female)"]

nets:
  N1: J1.pin3, OLED1.SDA
  N2: J1.pin10, OLED1.VDD
  N3: J2.pin2, OLED1.SCK
  N4: J2.pin4, OLED1.GND
  N5: IO0_GND_GND_RX_TX_5V.pin2, GND_CTS_VCC_TX_RX_DTR.pin5
  N6: IO0_GND_GND_RX_TX_5V.pin3, GND_CTS_VCC_TX_RX_DTR.pin4
  N7: IO0_GND_GND_RX_TX_5V.pin4, GND_CTS_VCC_TX_RX_DTR.pin1

notes:
  5v
  SD3
  G13 R8
  G14 R6
  G26 R4
  G33 R2
  G35
  SVN
  EN
  GND
  CMD
  SD2
  G12 R7
  G27 R5
  G25 R3
  G32 R1
  G34
  SVP
  3V3
  CLK
  SD1
  G2
  G4
  G17
  G18
  RXD
  G22
  3v3
  SD0
  G15
  G0
  G16
  G5
  G19
  G21
  TXD
  G23
  LED
  GND CTS VCC  TX  RX DTR
  GND VDD SCK SDA
